# Fritzing sketch LCD24C02EEPROM (saved by Fritzing 0.7.9b)
breadboards: 1

parts:
  LCD1 = LCD screen
  Arduino1 = Arduino
  R1 = Rotary Potentiometer (Large) [maximum_resistance=10kΩ package=THT]
  IC2 = 24LC02 [package=THT]
  R3 = Resistor [tolerance=±5% resistance=10k package=THT]
  R4 = Resistor [tolerance=±5% resistance=10k package=THT]

nets:
  VSS: LCD1.VSS, LCD1.R/W, Arduino1.GND, R1.leg2, IC2.A0, IC2.A1, IC2.A2, IC2.0V, IC2.WP_-_Write_Protect
  VDD: LCD1.VDD, Arduino1.+5V, R1.leg1, IC2.+V
  N1: LCD1.V0, R1.wiper
  N2: LCD1.RS, Arduino1.D12
  N3: LCD1.E, Arduino1.D11
  N4: LCD1.DB4, Arduino1.D5
  N5: LCD1.DB5, Arduino1.D4
  N6: LCD1.DB6, Arduino1.D3
  N7: LCD1.DB7, Arduino1.D2
  N8: Arduino1.A4, R3.Pin_0
  N9: Arduino1.A5, R4.Pin_1
  N10: IC2.SDA_-_I2C_Data, R3.Pin_1
  N11: IC2.SCL_-_I2C_Clock, R4.Pin_0
