# Fritzing sketch LCD_LM35 (saved by Fritzing 0.7.9b)
breadboards: 1

parts:
  LCD1 = LCD screen
  Arduino1 = Arduino
  LCD_V0 = Rotary Potentiometer (Large) [maximum_resistance=10kΩ package=THT]
  LM_35 = LM35 Temperature Sensor [package="TO92 [THT]"]

nets:
  GND: LCD1.VSS, LCD1.R/W, Arduino1.GND, LCD_V0.leg1, LM_35.GND
  VDD: LCD1.VDD, Arduino1.+5V, LCD_V0.leg2, LM_35.+Vs
  N1: LCD1.V0, LCD_V0.wiper
  N2: LCD1.RS, Arduino1.D12
  N3: LCD1.E, Arduino1.D11
  N4: LCD1.DB4, Arduino1.D5
  N5: LCD1.DB5, Arduino1.D4
  N6: LCD1.DB6, Arduino1.D3
  N7: LCD1.DB7, Arduino1.D2
  N8: Arduino1.A0, LM_35.Vout
