# Fritzing sketch LCD_potansiyometreli (saved by Fritzing 0.7.9b)
breadboards: 1

parts:
  LCD1 = LCD screen
  Arduino1 = Arduino
  R1 = Rotary Potentiometer (Large) [maximum_resistance=10kΩ package=THT]

nets (from the pcb view):
  N1: LCD1.V0, R1.wiper
  N2: LCD1.RS, Arduino1.D12
  N3: LCD1.R/W, Arduino1.GND, R1.leg1
  N4: LCD1.E, Arduino1.D11
  N5: LCD1.DB4, Arduino1.D5
  N6: LCD1.DB5, Arduino1.D4
  N7: LCD1.DB6, Arduino1.D3
  N8: Arduino1.+5V, R1.leg2
