# Fritzing sketch 24C02EEPROM (saved by Fritzing 0.7.9b)
breadboards: 1

parts:
  Arduino = Arduino
  IC1 = 24LC02 [package=THT]
  R1 = Resistor [tolerance=±5% resistance=10k package=THT]
  R2 = Resistor [tolerance=±5% resistance=10k package=THT]

nets:
  N1: Arduino.GND, IC1.A0, IC1.A1, IC1.A2, IC1.0V, IC1.WP_-_Write_Protect
  N2: Arduino.+5V, IC1.+V, R1.Pin_1, R2.Pin_1
  N3: Arduino.A4, IC1.SDA_-_I2C_Data, R1.Pin_0
  N4: Arduino.A5, IC1.SCL_-_I2C_Clock, R2.Pin_0
