# Fritzing sketch BC547Motor (saved by Fritzing 0.7.9b)
breadboards: 1

parts:
  R1 = Resistor [tolerance=±5% resistance=10k package=THT]
  Arduino1 = Arduino
  BC547 = NPN-Transistor [package="TO92 [THT]"]
  M1 = DC Motor
  R2 = Rotary Potentiometer (Large) [maximum_resistance=100kΩ package=THT]
  D1 = Rectifier Diode [part_number=1N4001 package="300 mil [THT]"]
  VCC1 = Battery block 9V

nets:
  N1: R1.Pin_0, Arduino1.D11
  N2: R1.Pin_1, BC547.B
  N3: Arduino1.GND, BC547.C, R2.leg1, VCC1.-
  N4: Arduino1.+5V, R2.leg2
  N5: Arduino1.A0, R2.wiper
  N6: BC547.E, M1.pin_1, D1.anode
  N7: M1.pin_2, D1.cathode, VCC1.+
