# Fritzing sketch LM35 (saved by Fritzing 0.7.9b)
breadboards: 1

parts:
  Arduino1 = Arduino
  T1 = LM35 Temperature Sensor [package="TO92 [THT]"]

nets:
  GND: Arduino1.GND, T1.GND
  N1: Arduino1.+5V, T1.+Vs
  N2: Arduino1.A0, T1.Vout
