# Fritzing sketch RGBLED (saved by Fritzing 0.7.9b)
breadboards: 1

parts:
  LED1 = RGB LED (com. cathode, rgb) [package="5 mm [THT]"]
  R1 = Resistor [tolerance=±5% resistance=470 package=THT]
  R3 = Resistor [tolerance=±5% resistance=470 package=THT]
  R4 = Resistor [tolerance=±5% resistance=470 package=THT]
  Arduino = Arduino

nets:
  N1: LED1.red_anode, R1.Pin_0
  N2: LED1.common_cathode, Arduino.+5V
  N3: LED1.green_anode, R4.Pin_0
  N4: LED1.blue_anode, R3.Pin_0
  N5: R1.Pin_1, Arduino.D10
  N6: R3.Pin_1, Arduino.D8
  N7: R4.Pin_1, Arduino.D9
