# Fritzing sketch SeriHaberlesme4LED (saved by Fritzing 0.7.9b)
breadboards: 1

parts:
  LED4 = Red LED - 5mm [package="5 mm [THT]"]
  Arduino1 = Arduino
  LED3 = Red LED - 5mm [package="5 mm [THT]"]
  LED2 = Red LED - 5mm [package="5 mm [THT]"]
  LED1 = Red LED - 5mm [package="5 mm [THT]"]
  R1 = Resistor [tolerance=±5% resistance=470 package=THT]
  R2 = Resistor [tolerance=±5% resistance=470 package=THT]
  R3 = Resistor [tolerance=±5% resistance=470 package=THT]
  R4 = Resistor [tolerance=±5% resistance=470 package=THT]

nets:
  N1: LED4.cathode, Arduino1.GND, LED3.cathode, LED2.cathode, LED1.cathode
  N2: LED4.anode, R4.Pin_0
  N3: Arduino1.D12, R1.Pin_1
  N4: Arduino1.D11, R2.Pin_1
  N5: Arduino1.D10, R3.Pin_1
  N6: Arduino1.D9, R4.Pin_1
  N7: LED3.anode, R3.Pin_0
  N8: LED2.anode, R2.Pin_0
  N9: LED1.anode, R1.Pin_0
