# Fritzing sketch potansiyometreOkuma (saved by Fritzing 0.7.9b)
breadboards: 1

parts:
  R1 = Rotary Potentiometer (Large) [maximum_resistance=100kΩ package=THT]
  Arduino1 = Arduino

nets:
  N1: R1.leg1, Arduino1.+5V
  N2: R1.wiper, Arduino1.A0
  N3: R1.leg2, Arduino1.GND
