# Fritzing sketch potansiyometrePWM (saved by Fritzing 0.7.9b)
breadboards: 1

parts:
  R1 = Rotary Potentiometer (Large) [maximum_resistance=100kΩ package=THT]
  Arduino1 = Arduino
  LED1 = LED - 5mm [color="Red (633nm)" package="5 mm [THT]"]
  R2 = Resistor [tolerance=±5% resistance=470 package=THT]

nets:
  N1: R1.leg1, Arduino1.+5V
  N2: R1.wiper, Arduino1.A0
  N3: R1.leg2, Arduino1.GND, LED1.cathode
  N4: Arduino1.D3, R2.Pin_1
  N5: LED1.anode, R2.Pin_0
