# Fritzing sketch 7Segment_Sayfa171 (saved by Fritzing 0.7.9b)
breadboards: 1

parts:
  Arduino1 = Arduino
  7_Segment = 7-Segment LED Display [package=THT]
  470 = Resistor [tolerance=±5% resistance=470 package=THT]
  470_2 = Resistor [tolerance=±5% resistance=470 package=THT]
  470_3 = Resistor [tolerance=±5% resistance=470 package=THT]
  470_4 = Resistor [tolerance=±5% resistance=470 package=THT]
  470_5 = Resistor [tolerance=±5% resistance=470 package=THT]
  470_6 = Resistor [tolerance=±5% resistance=470 package=THT]
  470_7 = Resistor [tolerance=±5% resistance=470 package=THT]

nets:
  N1: Arduino1.D6, 470_5.Pin_1
  N2: Arduino1.D5, 470_2.Pin_1
  N3: Arduino1.D4, 470.Pin_1
  N4: Arduino1.D3, 470_3.Pin_1
  N5: Arduino1.D2, 470_4.Pin_1
  N6: Arduino1.D1TX, 470_7.Pin_1
  N7: Arduino1.D0RX, 470_6.Pin_1
  N8: Arduino1.+5V, 7_Segment.commAnode#2
  N9: 7_Segment.cathodeE, 470.Pin_0
  N10: 7_Segment.cathodeD, 470_3.Pin_0
  N11: 7_Segment.cathodeC, 470_4.Pin_0
  N12: 7_Segment.cathodeB, 470_7.Pin_0
  N13: 7_Segment.cathodeA, 470_6.Pin_0
  N14: 7_Segment.cathodeF, 470_2.Pin_0
  N15: 7_Segment.cathodeG, 470_5.Pin_0
