# Fritzing sketch butonLed_sayfa143 (saved by Fritzing 0.7.9b)
breadboards: 1

parts:
  R1 = Resistor [tolerance=±5% resistance=10k package=THT]
  LED1 = LED - 5mm [color="Red (633nm)" package="5 mm [THT]"]
  R2 = Resistor [tolerance=±5% resistance=470 package=THT]
  Arduino1 = Arduino
  S3 = Pushbutton [package="[THT]"]

nets:
  N1: R1.Pin_0, Arduino1.D13, S3.Pin_1, S3.Pin_2
  N2: R1.Pin_1, R2.Pin_1, Arduino1.GND
  N3: LED1.cathode, R2.Pin_0
  N4: LED1.anode, Arduino1.D12
  N5: Arduino1.+5V, S3.Pin_3, S3.Pin_4
