# Fritzing sketch elektronikZarBreadboard_sayfa156 (saved by Fritzing 0.7.9b)
breadboards: 1

parts:
  R3 = Resistor [tolerance=±5% resistance=470 package=THT]
  R4 = Resistor [tolerance=±5% resistance=470 package=THT]
  R5 = Resistor [tolerance=±5% resistance=470 package=THT]
  R6 = Resistor [tolerance=±5% resistance=470 package=THT]
  R8 = Resistor [tolerance=±5% resistance=470 package=THT]
  10K = Resistor [tolerance=±5% resistance=470 package=THT]
  Arduino1 = Arduino
  LED12 = LED - 5mm [color="Red (633nm)" package="5 mm [THT]"]
  LED13 = LED - 5mm [color="Red (633nm)" package="5 mm [THT]"]
  LED14 = LED - 5mm [color="Red (633nm)" package="5 mm [THT]"]
  LED15 = LED - 5mm [color="Red (633nm)" package="5 mm [THT]"]
  LED16 = LED - 5mm [color="Red (633nm)" package="5 mm [THT]"]
  LED17 = LED - 5mm [color="Red (633nm)" package="5 mm [THT]"]
  LED18 = LED - 5mm [color="Red (633nm)" package="5 mm [THT]"]
  10K1 = Resistor [tolerance=±5% resistance=470 package=THT]
  R9 = Resistor [tolerance=±5% resistance=10k package=THT]
  S1 = Pushbutton [package="[THT]"]

nets:
  N1: R3.Pin_0, LED15.anode
  GND: R3.Pin_1, R4.Pin_1, R6.Pin_1, R8.Pin_1, 10K.Pin_0, Arduino1.GND, Arduino1.D7, Arduino1.D6, Arduino1.D4, Arduino1.D2, LED12.cathode, LED13.cathode, LED14.cathode, LED14.anode, LED15.cathode, LED16.cathode, LED17.cathode, LED18.cathode, R9.Pin_0
  N2: R4.Pin_0, LED12.anode
  N3: R5.Pin_0, LED17.anode
  N4: R5.Pin_1, Arduino1.D8
  N5: R6.Pin_0, Arduino1.D3
  N6: R8.Pin_0, LED13.anode
  N7: 10K.Pin_1, LED16.anode
  N8: Arduino1.D9, R9.Pin_1, S1.Pin_3, S1.Pin_4
  N9: Arduino1.D5, 10K1.Pin_1
  N10: Arduino1.+5V, S1.Pin_1, S1.Pin_2
  N11: LED18.anode, 10K1.Pin_0
