# Fritzing sketch karasimsek_Sayfa146 (saved by Fritzing 0.7.9b)
breadboards: 1

parts:
  Arduino1 = Arduino
  R2 = Resistor [tolerance=±5% resistance=470 package=THT]
  LED2 = LED - 5mm [color="Red (633nm)" package="5 mm [THT]"]
  LED3 = LED - 5mm [color="Red (633nm)" package="5 mm [THT]"]
  R4 = Resistor [tolerance=±5% resistance=470 package=THT]
  LED4 = LED - 5mm [color="Red (633nm)" package="5 mm [THT]"]
  R5 = Resistor [tolerance=±5% resistance=470 package=THT]
  LED5 = LED - 5mm [color="Red (633nm)" package="5 mm [THT]"]
  R6 = Resistor [tolerance=±5% resistance=470 package=THT]
  LED6 = LED - 5mm [color="Red (633nm)" package="5 mm [THT]"]
  R7 = Resistor [tolerance=±5% resistance=470 package=THT]
  R8 = Resistor [tolerance=±5% resistance=470 package=THT]
  LED7 = LED - 5mm [color="Red (633nm)" package="5 mm [THT]"]

nets:
  N1: Arduino1.GND, R2.Pin_1, R4.Pin_1, R5.Pin_1, R6.Pin_1, R7.Pin_1, R8.Pin_1
  N2: Arduino1.D13, LED7.anode
  N3: Arduino1.D12, LED2.anode
  N4: Arduino1.D11, LED3.anode
  N5: Arduino1.D10, LED6.anode
  N6: Arduino1.D9, LED4.anode
  N7: Arduino1.D8, LED5.anode
  N8: R2.Pin_0, LED7.cathode
  N9: LED2.cathode, R4.Pin_0
  N10: LED5.cathode, R8.Pin_0
